// Logisim project Self_stablizition_algorithem.circ as structural Verilog: 2 circuits, main circuit main
module main (
  input  in_1,
  input  in_2,
  input  in_3,
  input  in_4,
  input  in_5,
  input  in_6,
  input  in_7,
  input  in_8,
  input  in_9,
  input  in_10,
  input  in_11,
  input  in_12,
  input  in_13,
  input  in_14,
  input  in_15,
  input  in_16
);

  wire CLK, IRAM1, IRAM2, IRAM3, IRAM4, IRAM5, IRAM6, IRAM7, IRAM8, ORAM1, ORAM2, ORAM3, ORAM4, ORAM5, ORAM6,
       ORAM7, ORAM8, TOKEN0, TOKEN1, TOKEN2, TOKEN3, TOKEN4, TOKEN5, TOKEN6, TOKEN7, WRITE1, WRITE2, WRITE3,
       WRITE4, WRITE5, WRITE6, WRITE7, WRITE8;
  wire [7:0] cttr;

  LED led_1 (.in(TOKEN0));
  LED led_2 (.in(TOKEN0));
  LED led_3 (.in(TOKEN0));
  LED led_4 (.in(TOKEN0));
  RAM #(.dataWidth(1)) ram_1 (.addr(cttr), .we(WRITE1), .oe(WRITE1), .clk(CLK), .din(IRAM1), .dout(ORAM1));
  RAM #(.dataWidth(1)) ram_2 (.addr(cttr), .we(WRITE2), .oe(WRITE2), .clk(CLK), .din(IRAM2), .dout(ORAM2));
  LED led_5 (.in(TOKEN2));
  LED led_6 (.in(TOKEN2));
  LED led_7 (.in(TOKEN1));
  LED led_8 (.in(TOKEN1));
  LED led_9 (.in(TOKEN1));
  LED led_10 (.in(TOKEN2));
  LED led_11 (.in(TOKEN2));
  LED led_12 (.in(TOKEN1));
  // Probe on ORAM1
  // Probe on ORAM2
  // Probe on ORAM3
  // Probe on ORAM4
  // Probe on ORAM5
  // Probe on ORAM6
  // Probe on ORAM7
  // Probe on ORAM8
  LED led_13 (.in(TOKEN4));
  LED led_14 (.in(TOKEN4));
  LED led_15 (.in(TOKEN3));
  LED led_16 (.in(TOKEN3));
  LED led_17 (.in(TOKEN3));
  LED led_18 (.in(TOKEN4));
  LED led_19 (.in(TOKEN4));
  LED led_20 (.in(TOKEN3));
  LED led_21 (.in(TOKEN6));
  LED led_22 (.in(TOKEN6));
  LED led_23 (.in(TOKEN6));
  LED led_24 (.in(TOKEN5));
  LED led_25 (.in(TOKEN5));
  LED led_26 (.in(TOKEN5));
  LED led_27 (.in(TOKEN6));
  LED led_28 (.in(TOKEN5));
  Clock clock_1 (.out(CLK));
  RAM #(.dataWidth(1)) ram_3 (.addr(cttr), .we(WRITE3), .oe(WRITE3), .clk(CLK), .din(IRAM3), .dout(ORAM3));
  RAM #(.dataWidth(1)) ram_4 (.addr(cttr), .we(WRITE4), .oe(WRITE4), .clk(CLK), .din(IRAM4), .dout(ORAM4));
  LED led_29 (.in(TOKEN7));
  LED led_30 (.in(TOKEN7));
  LED led_31 (.in(TOKEN7));
  LED led_32 (.in(TOKEN7));
  RAM #(.dataWidth(1)) ram_5 (.addr(cttr), .we(WRITE5), .oe(WRITE5), .clk(CLK), .din(IRAM5), .dout(ORAM5));
  RAM #(.dataWidth(1)) ram_6 (.addr(cttr), .we(WRITE6), .oe(WRITE6), .clk(CLK), .din(IRAM6), .dout(ORAM6));
  RAM #(.dataWidth(1)) ram_7 (.addr(cttr), .we(WRITE7), .oe(WRITE7), .clk(CLK), .din(IRAM7), .dout(ORAM7));
  RAM #(.dataWidth(1)) ram_8 (.addr(cttr), .we(WRITE8), .oe(WRITE8), .clk(CLK), .din(IRAM8), .dout(ORAM8));
  ControlSystem controlsystem_1 (
    .in_1(in_1), .in_2(in_3), .in_3(in_5), .in_4(in_7), .in_5(in_9), .in_6(in_11), .in_7(in_13),
    .in_8(in_15), .in_9(in_2), .in_10(in_4), .in_11(in_6), .in_12(in_8), .in_13(in_10), .in_14(in_12),
    .in_15(in_14), .in_16(in_16), .in_17(ORAM1), .in_18(ORAM2), .in_19(ORAM3), .in_20(ORAM4), .in_21(ORAM5),
    .in_22(ORAM6), .in_23(ORAM7), .in_24(ORAM8), .TONEK0(TOKEN0), .TONEK1(TOKEN1), .TONEK2(TOKEN2),
    .TONEK3(TOKEN3), .TONEK4(TOKEN4), .TONEK5(TOKEN5), .TONEK6(TOKEN6), .TONEK7(TOKEN7), .WRITE1(WRITE1),
    .WRITE2(WRITE2), .WRITE3(WRITE3), .WRITE4(WRITE4), .out_37(WRITE5), .out_38(WRITE6), .out_39(WRITE7),
    .out_40(WRITE8), .IRAM1(IRAM1), .IRAM2(IRAM2), .IRAM3(IRAM3), .IRAM4(IRAM4), .IRAM5(IRAM5),
    .IRAM6(IRAM6), .out_47(IRAM7), .out_48(IRAM8));
  Counter counter_1 (.clk(CLK), .Q(cttr));  // open: clr, load, up, count, D, carry

  // Other names for the same wires on the sheet: centralDemon0 = in_2; centralDemon1 = in_4; centralDemon2 = in_6;
  //   centralDemon3 = in_8; centralDemon4 = in_10; centralDemon5 = in_12; centralDemon6 = in_14;
  //   centralDemon7 = in_16; user0 = in_1; user1 = in_3; user2 = in_5; user3 = in_7; user4 = in_9; user5 = in_11;
  //   user6 = in_13; user7 = in_15
endmodule

module ControlSystem (
  input  in_1,
  input  in_2,
  input  in_3,
  input  in_4,
  input  in_5,
  input  in_6,
  input  in_7,
  input  in_8,
  input  in_9,
  input  in_10,
  input  in_11,
  input  in_12,
  input  in_13,
  input  in_14,
  input  in_15,
  input  in_16,
  input  in_17,
  input  in_18,
  input  in_19,
  input  in_20,
  input  in_21,
  input  in_22,
  input  in_23,
  input  in_24,
  output TONEK0,
  output TONEK1,
  output TONEK2,
  output TONEK3,
  output TONEK4,
  output TONEK5,
  output TONEK6,
  output TONEK7,
  output WRITE1,
  output WRITE2,
  output WRITE3,
  output WRITE4,
  output out_37,
  output out_38,
  output out_39,
  output out_40,
  output IRAM1,
  output IRAM2,
  output IRAM3,
  output IRAM4,
  output IRAM5,
  output IRAM6,
  output out_47,
  output out_48
);

  wire CHANGE1, CHANGE2, CHANGE3, CHANGE4, CHANGE5, CHANGE6, CHANGE7, CHANGE8, enable0, enable1, enable2,
       enable3, enable4, enable5, enable6, enable7, or_1_out, or_2_out, or_3_out, or_4_out, or_5_out,
       or_6_out, or_7_out, or_8_out, xnor_1_out, xnor_2_out, xnor_3_out, xnor_4_out, xnor_5_out, xnor_6_out,
       xor_1_out, xor_2_out, xor_3_out, xor_4_out, xor_5_out, xor_6_out, xor_7_out, xor_8_out, xor_9_out,
       xor_10_out, xor_11_out, xor_12_out;

  or or_1 (or_1_out, in_1, TONEK0);
  or or_2 (or_2_out, in_2, TONEK1);
  and and_1 (IRAM1, CHANGE1, 1'b1);
  and and_2 (IRAM2, CHANGE2, 1'b1);
  assign CHANGE1 = enable0 ? ~in_17 : 1'bz;  // Controlled_Inverter controlled_inverter_1
  assign CHANGE2 = enable1 ? ~in_18 : 1'bz;  // Controlled_Inverter controlled_inverter_2
  xnor xnor_1 (xnor_1_out, in_17, in_18);
  xnor xnor_2 (xnor_2_out, in_18, in_19);
  xor xor_1 (xor_1_out, in_18, in_20);
  xnor xnor_3 (xnor_3_out, in_19, in_20);
  xnor xnor_4 (xnor_4_out, in_20, in_21);
  xor xor_2 (xor_2_out, in_20, in_22);
  xnor xnor_5 (xnor_5_out, in_21, in_22);
  xnor xnor_6 (xnor_6_out, in_22, in_23);
  xor xor_3 (xor_3_out, in_22, in_24);
  xnor xnor_7 (TONEK7, in_23, in_24);
  and and_3 (WRITE1, or_1_out, in_9);
  and and_4 (WRITE2, or_2_out, in_10);
  and and_5 (TONEK1, xnor_1_out, xnor_2_out, xor_1_out);
  and and_6 (TONEK3, xnor_3_out, xnor_4_out, xor_2_out);
  and and_7 (TONEK5, xnor_5_out, xnor_6_out, xor_3_out);
  and and_8 (IRAM3, CHANGE3, 1'b1);
  and and_9 (IRAM4, CHANGE4, 1'b1);
  assign CHANGE3 = enable2 ? ~in_19 : 1'bz;  // Controlled_Inverter controlled_inverter_3
  assign CHANGE4 = enable3 ? ~in_20 : 1'bz;  // Controlled_Inverter controlled_inverter_4
  or or_3 (or_3_out, in_4, TONEK3);
  or or_4 (or_4_out, in_3, TONEK2);
  assign CHANGE5 = enable4 ? ~in_21 : 1'bz;  // Controlled_Inverter controlled_inverter_5
  assign CHANGE6 = enable5 ? ~in_22 : 1'bz;  // Controlled_Inverter controlled_inverter_6
  and and_10 (IRAM5, CHANGE5, 1'b1);
  and and_11 (IRAM6, CHANGE6, 1'b1);
  and and_12 (WRITE3, or_4_out, in_11);
  and and_13 (WRITE4, or_3_out, in_12);
  xor xor_4 (xor_4_out, in_17, in_19);
  xor xor_5 (xor_5_out, in_19, in_18);
  xor xor_6 (xor_6_out, in_19, in_20);
  xor xor_7 (xor_7_out, in_19, in_21);
  xor xor_8 (xor_8_out, in_21, in_20);
  xor xor_9 (xor_9_out, in_21, in_22);
  xor xor_10 (xor_10_out, in_24, in_23);
  xor xor_11 (xor_11_out, in_23, in_21);
  xor xor_12 (xor_12_out, in_23, in_22);
  xor xor_13 (TONEK0, in_17, in_18);
  assign CHANGE7 = enable6 ? ~in_23 : 1'bz;  // Controlled_Inverter controlled_inverter_7
  assign CHANGE8 = enable7 ? ~in_24 : 1'bz;  // Controlled_Inverter controlled_inverter_8
  or or_5 (or_5_out, in_5, TONEK4);
  and and_14 (TONEK2, xor_4_out, xor_5_out, xor_6_out);
  and and_15 (TONEK4, xor_7_out, xor_8_out, xor_9_out);
  and and_16 (TONEK6, xor_10_out, xor_11_out, xor_12_out);
  or or_6 (or_6_out, in_6, TONEK5);
  and and_17 (out_47, CHANGE7, 1'b1);
  and and_18 (out_48, CHANGE8, 1'b1);
  and and_19 (out_37, or_5_out, in_13);
  and and_20 (out_38, or_6_out, in_14);
  and and_21 (enable0, in_9, TONEK0);
  and and_22 (enable1, in_10, TONEK1);
  and and_23 (enable2, in_11, TONEK2);
  or or_7 (or_7_out, in_7, TONEK6);
  or or_8 (or_8_out, in_8, TONEK7);
  and and_24 (out_39, or_7_out, in_15);
  and and_25 (out_40, or_8_out, in_16);
  and and_26 (enable3, in_12, TONEK3);
  and and_27 (enable4, in_13, TONEK4);
  and and_28 (enable5, in_14, TONEK5);
  and and_29 (enable6, in_15, TONEK6);
  and and_30 (enable7, in_16, TONEK7);

  // Other names for the same wires on the sheet: centralDemon0 = in_9; centralDemon1 = in_10; centralDemon2 = in_11;
  //   centralDemon3 = in_12; centralDemon4 = in_13; centralDemon5 = in_14; centralDemon6 = in_15;
  //   centralDemon7 = in_16; IRAM7 = out_47; IRAM8 = out_48; ORAM1 = in_17; ORAM2 = in_18; ORAM3 = in_19;
  //   ORAM4 = in_20; ORAM5 = in_21; ORAM6 = in_22; ORAM7 = in_23; ORAM8 = in_24; user0 = in_1; user1 = in_2;
  //   user2 = in_3; user3 = in_4; user4 = in_5; user5 = in_6; user6 = in_7; user7 = in_8; WRITE5 = out_37;
  //   WRITE6 = out_38; WRITE7 = out_39; WRITE8 = out_40; TOKEN0 = TONEK0; XOR1 = TONEK0; TOKEN1 = TONEK1;
  //   XOR2 = TONEK1; TOKEN2 = TONEK2; XOR3 = TONEK2; TOKEN3 = TONEK3; XOR4 = TONEK3; TOKEN4 = TONEK4; XOR5 = TONEK4;
  //   TOKEN5 = TONEK5; XOR6 = TONEK5; TOKEN6 = TONEK6; XOR7 = TONEK6; TOKEN7 = TONEK7; XOR8 = TONEK7
endmodule
